# Fritzing sketch ESP8266 Coffee (saved by Fritzing 0.9.2b)
breadboards: 1

parts:
  Part1 = HUZZAH ESP8266 Breakout
  IC1 = DIP - 16 pins [chip_label=MCP3208 package="DIP (Dual Inline) [THT]"]
  U1 = Optocoupler [package=THT]
  U3 = RELAY-SOLIDSTATE [package=relay-s108t02]
  C1 = Ceramic Capacitor [capacitance=1µF package="100 mil [THT, multilayer]"]
  C3 = Ceramic Capacitor [capacitance=1µF package="100 mil [THT, multilayer]"]
  R1 = Resistor [tolerance=±5% resistance=10k package=THT]
  Grove1 = Grove Temperature Sensor
  Grove2 = Grove Temperature Sensor
  R2 = Resistor [tolerance=±5% resistance=220 package=THT]
  Power_plug1 = Power plug

nets:
  N1: Part1.GPIO14, IC1.CLC
  N2: Part1.GPIO12, IC1.Dout_MISO
  N3: Part1.GPIO13, IC1.Din_MOSI
  GND: Part1.GND, IC1.DGND, IC1.AGN, U1.Pin_2, U1.Pin_5, C1.1, C3.0, Grove1.GND, Grove2.GND, Power_plug1.GND
  VCC: Part1.3.3V, IC1.Vref, IC1.Vdd, U3.+, C1.0, C3.1, R1.Pin_1, Grove1.VCC, Grove2.VCC, Power_plug1.VCC
  N4: Part1.GPIO2, R2.Pin_0
  N5: IC1.Chan0, Grove2.SIG
  N6: IC1.Chan1, Grove1.SIG
  N7: IC1.CS, R1.Pin_0
  N8: U1.Pin_1, R2.Pin_1
  N9: U1.Pin_4, U3.-

notes:
  Fake High Temperature Sensor - two analog outputs
  High-Side Switch?
  Inversion?

custom parts:
  HUZZAH ESP8266 Breakout: The ESP8266 processor from Espressif is an 80 MHz microcontroller with a full WiFi front-end (both as client and access point) and TCP/IP stack with DNS support as well.
  DIP - 16 pins: A DIP stand-in part for whatever IC you want. With 16 pins on a 300mil dual inline package (DIP) footprint.
